# Fritzing sketch rpi-neocam (saved by Fritzing 0.9.0b)
breadboards: 1

parts:
  S1 = Momentary Switch [package=ksa_sealed_tac_switch]
  R1 = Resistor [package="2010 [SMD]"]
  J1 = Cobbler Plus
  JACK3 = 2.1mm Barrel Jack with Terminal Block
  74AHC3 = SN74AHC125
  Neopixel_Ring_16 = Neopixel Ring 16
  Neopixel_Stick_8 = Neopixel Strip -- Black (60/m)

nets:
  N1: S1.2, R1.Pin_1, J1.EEC
  N2: S1.4, J1.SCLK
  N3: R1.Pin_0, J1.3V3, J1.5.0V
  N4: J1.SCL, JACK3.NEG, 74AHC3.1OE, 74AHC3.GND, Neopixel_Stick_8.GND#3
  N5: J1.CE1, 74AHC3.1A
  N6: JACK3.POS, 74AHC3.VCC, Neopixel_Stick_8.DI
  N7: 74AHC3.1Y, Neopixel_Stick_8.+5V#1
  N8: Neopixel_Ring_16.GND, Neopixel_Stick_8.GND#4
  N9: Neopixel_Ring_16.VCC, Neopixel_Stick_8.DO
  N10: Neopixel_Ring_16.IN, Neopixel_Stick_8.+5V#6

notes:
  5v 2A DC
  Plus additional Neopixel stick 8
  (connected after Neopixel ring 16)
  As follows:
  stick(8) -> ring(16) -> stick(8)

custom parts:
  Cobbler Plus: The Cobbler Plus is an add on prototyping board from Adafruit specifically designed for the Raspberry Pi B+ that can break out all those tasty power, GPIO, I2C and SPI pins from the 40-pin header onto a solderless breadboard. This set will make "cobbling together" prototypes with the Pi super easy. The Cobbler Plus can plug into any solderless breadboard.
  SN74AHC125: Quad Buffer/Line Driver, 3 State. Inputs Outputs xOE xA xY L L L L H H H X Z Where L = low, H = high, X = don't care, Z = high impedence OFF state
  Neopixel Ring 16: Neopixel Ring x16
  Neopixel Strip -- Black (60/m): Neopixel Strip, Black, 60 pixels per meter.
