# Fritzing sketch rpi-neopixels-5v (saved by Fritzing 0.9.0b)
breadboards: 1

parts:
  J3 = Cobbler Plus
  Neopixel_Ring_16 = Neopixel Ring 16
  Neopixel_Stick_8 = Neopixel Strip -- Black (60/m)
  JACK2 = 2.1mm Barrel Jack with Terminal Block
  74AHC2 = SN74AHC125

nets:
  N1: J3.SCL, Neopixel_Stick_8.GND#3, JACK2.NEG, 74AHC2.1OE, 74AHC2.GND
  N2: J3.CE1, 74AHC2.1A
  N3: Neopixel_Ring_16.GND, Neopixel_Stick_8.GND#4
  N4: Neopixel_Ring_16.VCC, Neopixel_Stick_8.DO
  N5: Neopixel_Ring_16.IN, Neopixel_Stick_8.+5V#6
  N6: Neopixel_Stick_8.+5V#1, 74AHC2.1Y
  N7: Neopixel_Stick_8.DI, JACK2.POS, 74AHC2.VCC

notes:
  5v 2A DC

custom parts:
  Cobbler Plus: The Cobbler Plus is an add on prototyping board from Adafruit specifically designed for the Raspberry Pi B+ that can break out all those tasty power, GPIO, I2C and SPI pins from the 40-pin header onto a solderless breadboard. This set will make "cobbling together" prototypes with the Pi super easy. The Cobbler Plus can plug into any solderless breadboard.
  Neopixel Ring 16: Neopixel Ring x16
  Neopixel Strip -- Black (60/m): Neopixel Strip, Black, 60 pixels per meter.
  SN74AHC125: Quad Buffer/Line Driver, 3 State. Inputs Outputs xOE xA xY L L L L H H H X Z Where L = low, H = high, X = don't care, Z = high impedence OFF state
